// Digital circuit 6502.dig as structural Verilog
module _6502 (
  input  in_1,
  input  clk,
  input  in_3,
  input  [7:0] in_6,
  input  [7:0] in_7,
  input  [2:0] in_8,
  input  [15:0] PC_Data,
  output out_4,
  output out_5,
  output out_9,
  output [15:0] out_10,
  output [7:0] out_11
);

  wire [15:0] program_counter_custom_1_p5;

  // Program_Counter_custom program_counter_custom_1: pin names not known; wires that end beside it: in_1, in_3, clk, out_4, program_counter_custom_1_p5, in_6, in_7, in_8
  assign program_counter_custom_1_p5 = in_1 ? PC_Data : 16'bz;  // Driver driver_1
  assign out_10 = ~in_1 ? program_counter_custom_1_p5 : 16'bz;  // DriverInvSel driverinvsel_1
  ALU_custom alu_custom_1 ();
endmodule
